// Logisim project Ula.circ as structural Verilog: 1 circuit, main circuit main
module main (
  input  AInv,
  input  BInv,
  input  Cin,
  input  A,
  input  [2:0] in_5,
  input  B
);

  wire adder_1_cout, adder_1_out, and_1_out, multiplexer_1_out, multiplexer_2_out, multiplexer_3_out,
       nor_1_out, not_1_out, not_2_out, or_1_out, xor_1_out;

  not not_1 (not_1_out, A);
  Multiplexer multiplexer_1 (.in0(A), .in1(not_1_out), .out(multiplexer_1_out), .sel(AInv));  // open: en
  not not_2 (not_2_out, B);
  Multiplexer multiplexer_2 (.in0(B), .in1(not_2_out), .out(multiplexer_2_out), .sel(BInv));  // open: en
  and and_1 (and_1_out, multiplexer_1_out, multiplexer_2_out);
  or or_1 (or_1_out, multiplexer_1_out, multiplexer_2_out);
  xor xor_1 (xor_1_out, multiplexer_1_out, multiplexer_2_out);
  nor nor_1 (nor_1_out, multiplexer_1_out, multiplexer_2_out);
  Adder #(.width(1)) adder_1 (
    .a(multiplexer_1_out), .b(multiplexer_2_out), .out(adder_1_out), .cin(Cin), .cout(adder_1_cout));
  // Probe on adder_1_cout
  Multiplexer #(.select(3)) multiplexer_3 (
    .in0(and_1_out), .in1(or_1_out), .in2(xor_1_out), .in3(nor_1_out), .in4(adder_1_out),
    .out(multiplexer_3_out), .sel(in_5), .en(1'b1));  // open: in5, in6, in7
  // Probe on multiplexer_3_out
endmodule
